# Fritzing sketch Joystick_Circuito_Fritzing (saved by Fritzing 0.9.3b)
circuit board: 8.46667cm x 5.64444cm

parts:
  Componente1 = Arduino Uno (Rev3) - ICSP
  Switch_Modo_Carretera = Toggle Switch [package=THT]
  R1 = Resistor [tolerance=±5% resistance=2.2k package=THT]
  R3 = Resistor [tolerance=±5% resistance=2.2k package=THT]
  Btn_Bajar_Palanca = SWITCH-MOMENTARY-2 [package=tactile-switch-1101ne]
  Btn_Subir_Palanca = SWITCH-MOMENTARY-2 [package=tactile-switch-1101ne]
  Btn_Fijar_Freno = SWITCH-MOMENTARY-2 [package=tactile-switch-1101ne]
  ATX_Conector_6pin2 = ATX_Conector_6pin [part_number=23LCV1024]
  Conector_Joystick_ATX1 = ATX_Conector_6pin [part_number=23LCV1024]
  Conecotor_Joystick_ATX_2 = ATX_Conector_6pin [part_number=23LCV1024]
  ATX_Conector_6pin4 = ATX_Conector_6pin [part_number=23LCV1024]
  R4 = Resistor [tolerance=±5% resistance=2.2k package=THT]
  JP2 = Header 10 [package=1x10-2mm-smd]
  JP1 = Header 10 [package=1x10-2mm-smd]
  R9 = Resistor [tolerance=±5% resistance=2.2k package=THT]
  ATX_Conector_6pin5 = ATX_Conector_6pin [part_number=23LCV1024]
  Joystick_Y = Rotary Potentiometer (Small) [maximum_resistance=100kΩ package=THT]
  Joystick_X = Rotary Potentiometer (Small) [maximum_resistance=100kΩ package=THT]
  ATX_Conector_6pin3 = ATX_Conector_6pin [part_number=23LCV1024]

nets:
  N1: Componente1.A0, ATX_Conector_6pin4.P6
  N2: Componente1.A1, ATX_Conector_6pin4.P3
  N3: Componente1.A4/SDA, ATX_Conector_6pin4.P5
  N4: Componente1.A5/SCL, ATX_Conector_6pin4.P2
  N5: Componente1.D10_PWM/SS, ATX_Conector_6pin3.P2
  N6: Componente1.D11_PWM/MOSI, ATX_Conector_6pin3.P5
  N7: Componente1.D2, ATX_Conector_6pin3.P4
  N8: Componente1.D3_PWM, ATX_Conector_6pin3.P1
  N9: Switch_Modo_Carretera.L1, Switch_Modo_Carretera.COM
  N10: Switch_Modo_Carretera.L2, JP2.4
  N11: R1.Pin_0, R3.Pin_0, ATX_Conector_6pin2.P1, ATX_Conector_6pin2.P4, Conector_Joystick_ATX1.P1, R4.Pin_0, R9.Pin_0
  N12: R1.Pin_1, Conecotor_Joystick_ATX_2.P2, JP1.5
  N13: R3.Pin_1, Conector_Joystick_ATX1.P5, JP1.2
  N14: Btn_Bajar_Palanca.2, JP2.2
  N15: Btn_Subir_Palanca.2, JP2.5
  N16: Btn_Fijar_Freno.1, JP2.1
  N17: Btn_Fijar_Freno.2, JP2.3
  N18: ATX_Conector_6pin2.P2, Conecotor_Joystick_ATX_2.P3
  N19: ATX_Conector_6pin2.P3, ATX_Conector_6pin2.P6, Conector_Joystick_ATX1.P4, JP1.1
  N20: ATX_Conector_6pin2.P5, Conecotor_Joystick_ATX_2.P6
  N21: Conector_Joystick_ATX1.P2, R4.Pin_1, JP1.3
  N22: Conecotor_Joystick_ATX_2.P5, JP1.4, R9.Pin_1
  N23: ATX_Conector_6pin5.P1, Joystick_Y.leg2
  N24: ATX_Conector_6pin5.P2, Joystick_X.wiper
  N25: ATX_Conector_6pin5.P3, Joystick_Y.leg1
  N26: ATX_Conector_6pin5.P4, Joystick_X.leg2
  N27: ATX_Conector_6pin5.P5, Joystick_Y.wiper
  N28: ATX_Conector_6pin5.P6, Joystick_X.leg1

custom parts:
  ATX_Conector_6pin: Serial SRAM
