# Fritzing sketch Joystick_Circuito (saved by Fritzing 0.9.3b)
circuit board: 8.46667cm x 5.64444cm
breadboards: 1

parts:
  PCF = PCF8574 [package="DIP16 [THT]"]
  Componente1 = Arduino Uno (Rev3) - ICSP
  LED1 = LED - 3mm [color="Red (633nm)" package="3 mm [THT]"]
  LED2 = LED - 3mm [color="Red (633nm)" package="3 mm [THT]"]
  LED3 = LED - 3mm [color="Red (633nm)" package="3 mm [THT]"]
  LED4 = LED - 3mm [color="Red (633nm)" package="3 mm [THT]"]
  Switch_Fijar_Freno = Toggle Switch [package=THT]
  R1 = Resistor [tolerance=±5% resistance=2.2k package=THT]
  R2 = Resistor [tolerance=±5% resistance=2.2k package=THT]
  R4 = Resistor [tolerance=±5% resistance=2.2k package=THT]
  R5 = Resistor [tolerance=±5% resistance=220 package=THT]
  R6 = Resistor [tolerance=±5% resistance=220 package=THT]
  R7 = Resistor [tolerance=±5% resistance=220 package=THT]
  R8 = Resistor [tolerance=±5% resistance=220 package=THT]
  R3 = Resistor [tolerance=±5% resistance=4.7k package=THT]
  S6 = SWITCH-MOMENTARY-2 [package=tactile-switch-1101ne]  # not connected
  S5 = SWITCH-MOMENTARY-2 [package=tactile-switch-1101ne]
  S4 = SWITCH-MOMENTARY-2 [package=tactile-switch-1101ne]  # not connected

nets:
  N1: PCF.P0, Switch_Fijar_Freno.L1, R1.Pin_0
  N2: PCF.P1, R2.Pin_0
  N3: PCF.P2, R3.Pin_0, S5.2
  N4: PCF.P3, R4.Pin_0
  GND: PCF.GND, Componente1.GND, Switch_Fijar_Freno.COM
  N5: PCF.P4, R8.Pin_0
  N6: PCF.P5, R7.Pin_0
  N7: PCF.P6, R6.Pin_0
  N8: PCF.P7, R5.Pin_0
  VCC: PCF.VCC, Componente1.5V, LED1.anode, LED2.anode, LED3.anode, LED4.anode, R1.Pin_1, R2.Pin_1, R4.Pin_1, R3.Pin_1
  N9: LED1.cathode, R8.Pin_1
  N10: LED2.cathode, R7.Pin_1
  N11: LED3.cathode, R6.Pin_1
  N12: LED4.cathode, R5.Pin_1

notes:
  VDD SDA SCL INT P7 P6 P5 P4
  A0 A1 A2 P0 P1 P2 P3 VSS
