# Fritzing sketch DiagramaGeneral (saved by Fritzing 0.9.3b)
circuit board: 8.46667cm x 5.64444cm
breadboards: 1

parts:
  Arduino_UNO = Arduino Uno (Rev3)
  Joystick_Sparkfun_Azul=>TapCentral = JOYSTICK-PSP1000 [package=joystick-psp1000]
  Puente_H_Freno_(Addr_0x0D) = Pololu 24v23 Motor Driver
  Feedback_Actuator_1_(Freno) = SLIDER [package=slider]
  Feedback_Actuator_2_(Acelerador) = SLIDER [package=slider]
  Puente_H_Acel_(Addr_0x0A) = Pololu 24v23 Motor Driver
  Actuador_ServoCity_(A2) = Solenoid
  Actuador_ServoCity_(A1) = Solenoid
  Bateria_12V = Battery Holders [package=battery_20mm_pth_compact]
  IC1 = 25LC1024 [package=THT]
  Puente_H_Volante_(Addr_0x) = Pololu 24v23 Motor Driver
  Actuador_ServoCity_(A2)1 = Solenoid  # not connected
  Actuador_ServoCity_(A2)3 = Solenoid  # not connected
  U1 = PCF8574 [package="DIP16 [THT]"]
  Botón_mapeo_completo_volante = Pushbutton [package=THT]
  R1 = Resistor [tolerance=±5% resistance=220 package=THT]
  R2 = Resistor [tolerance=±5% resistance=220 package=THT]
  R3 = Resistor [tolerance=±5% resistance=220 package=THT]
  R4 = Resistor [tolerance=±5% resistance=220 package=THT]  # not connected
  LED1 = smd LED [color="Yellow (595nm)" package="0805 [SMD]"]
  LED2 = smd LED [color="Yellow (595nm)" package="0805 [SMD]"]
  LED3 = smd LED [color="Red (633nm)" package="0805 [SMD]"]
  LED4 = smd LED [color="Red (633nm)" package="0805 [SMD]"]
  Switch_mapeo_completo_Acelerador = SWITCH_SPDT [package=kps-1290]
  JP3 = Header 3 [package=screwterminal-3.5mm-3_lock.007s]  # not connected
  JP4 = Header 3 [package=screwterminal-3.5mm-3_lock.007s]  # not connected
  JP5 = Header 3 [package=screwterminal-3.5mm-3_lock.007s]  # not connected
  JP6 = Header 3 [package=screwterminal-3.5mm-3_lock.007s]  # not connected
  J1 = AVR ISP 6 Pin [package=2x3-ns]  # not connected

nets:
  N1: Arduino_UNO.A0, Joystick_Sparkfun_Azul=>TapCentral.Y
  N2: Arduino_UNO.A1, Joystick_Sparkfun_Azul=>TapCentral.X
  N3: Arduino_UNO.A2, Feedback_Actuator_1_(Freno).S
  N4: Arduino_UNO.A3, Feedback_Actuator_2_(Acelerador).S
  N5: Arduino_UNO.D8, Puente_H_Freno_(Addr_0x0D).Rx
  N6: Arduino_UNO.D10_PWM/SS, IC1.CS_-_Chip_Select
  N7: Arduino_UNO.D11_PWM/MOSI, IC1.SI_-_Data_In
  N8: Arduino_UNO.D12/MISO, IC1.SO_-_Data_Out, IC1.WP_-_Write_Protect
  N9: Arduino_UNO.D13/SCK, IC1.SCK_-_SPI_Clock
  5V: Arduino_UNO.5V, Joystick_Sparkfun_Azul=>TapCentral.VCC, Feedback_Actuator_1_(Freno).A
  GND: Arduino_UNO.GND, Joystick_Sparkfun_Azul=>TapCentral.GND, Puente_H_Freno_(Addr_0x0D).GND#0, Feedback_Actuator_1_(Freno).E, Puente_H_Acel_(Addr_0x0A).GND#0, IC1.0V
  N10: Puente_H_Freno_(Addr_0x0D).GND#6, Puente_H_Acel_(Addr_0x0A).GND#6, Bateria_12V.-
  N11: Puente_H_Freno_(Addr_0x0D).OUT_A, Actuador_ServoCity_(A1).pin2
  N12: Puente_H_Freno_(Addr_0x0D).OUT_B, Actuador_ServoCity_(A1).pin1
  VIN: Puente_H_Freno_(Addr_0x0D).VIn, Puente_H_Acel_(Addr_0x0A).VIn, Bateria_12V.+
  N13: Puente_H_Acel_(Addr_0x0A).OUT_A, Actuador_ServoCity_(A2).pin2
  N14: Puente_H_Acel_(Addr_0x0A).OUT_B, Actuador_ServoCity_(A2).pin1
  N15: IC1.HOLD, IC1.+V, R1.Pin_1, R2.Pin_1, R3.Pin_1
  N16: Puente_H_Volante_(Addr_0x).OUT_A, Puente_H_Volante_(Addr_0x).OUT_B
  N17: U1.P0, Botón_mapeo_completo_volante.leg1
  N18: U1.P1, Switch_mapeo_completo_Acelerador.O
  N19: U1.P4, LED4.cathode
  N20: U1.P5, LED3.cathode
  N21: U1.P6, LED2.cathode
  N22: U1.P7, LED1.cathode

custom parts:
  Pololu 24v23 Motor Driver: DC Motor Driver from Pololu
